// Logisim project mata3820171.circ as structural Verilog: 1 circuit, main circuit main
module main (
  input  [1:0] in_1,
  input  [1:0] in_2,
  output [7:0] R0,
  output [7:0] R1,
  output [7:0] R2,
  output [7:0] R3,
  output [7:0] out_7,
  output [7:0] out_8,
  output [7:0] out_9,
  output [7:0] out_10,
  output [7:0] out_11,
  output [7:0] out_12,
  output [7:0] out_13,
  output [7:0] out_14,
  output [7:0] out_15,
  output [7:0] out_16,
  output [7:0] out_17,
  output [7:0] out_18,
  output [7:0] out_19,
  output [7:0] out_20,
  output [7:0] out_21,
  output [7:0] out_22,
  output [7:0] out_23,
  output [7:0] out_24,
  output [7:0] out_25,
  output [7:0] out_26,
  output [7:0] out_27,
  output [7:0] out_28,
  output [7:0] out_29,
  output [7:0] out_30,
  output [7:0] out_31,
  output [7:0] out_32,
  output [7:0] out_33,
  output [7:0] out_34,
  output [7:0] out_35,
  output [7:0] out_36,
  output [7:0] out_37,
  output [7:0] out_38
);

  wire [7:0] multiplexer_1_out, multiplexer_2_out;

  Multiplexer #(.select(2), .width(8)) multiplexer_1 (
    .in0(R0), .in1(R1), .in2(R2), .in3(R3), .out(multiplexer_1_out), .sel(in_1));  // open: en
  Multiplexer #(.select(2), .width(8)) multiplexer_2 (
    .in0(R0), .in1(R1), .in2(R2), .out(multiplexer_2_out), .sel(in_2));  // open: in3, en
  Demultiplexer #(.select(4), .width(8)) demultiplexer_1 (
    .out0(out_7), .out1(out_8), .out2(out_9), .out3(out_10), .out4(out_11), .out5(out_12), .out6(out_13),
    .out7(out_14), .out8(out_15), .out9(out_16), .out10(out_17), .out11(out_18), .out12(out_19),
    .out13(out_20), .out14(out_21), .out15(out_22), .in(multiplexer_2_out), .sel(4'b1111));  // open: en
  Demultiplexer #(.select(4), .width(8)) demultiplexer_2 (
    .out0(out_23), .out1(out_24), .out2(out_25), .out3(out_26), .out4(out_27), .out5(out_28), .out6(out_29),
    .out7(out_30), .out8(out_31), .out9(out_32), .out10(out_33), .out11(out_34), .out12(out_35),
    .out13(out_36), .out14(out_37), .out15(out_38), .in(multiplexer_1_out), .sel(4'b1111));  // open: en
endmodule
